# Fritzing sketch ControladorDeCarga (saved by Fritzing 0.9.3b)

parts:
  Componente1 = Arduino Uno (Rev3)
  Componente2 = Voltage Sensor 25V
  ZS-042_RTC1 = ZS-042 RTC Module
  OLED_I2C1 = OLED 128x64 I2C Monochrome Display
  S1 = Momentary Switch [package=ksa_sealed_tac_switch]
  C1 = Capacitor [part_number=104 package=cap-pth-small2]
  R1 = Resistor [tolerance=±5% resistance=10k package="2010 [SMD]"]
  S2 = Momentary Switch [package=ksa_sealed_tac_switch]
  S3 = Momentary Switch [package=ksa_sealed_tac_switch]
  C2 = Capacitor [part_number=104 package=cap-pth-small2]
  C3 = Capacitor [part_number=104 package=cap-pth-small2]
  R2 = Resistor [tolerance=±5% resistance=10k package="2010 [SMD]"]
  R3 = Resistor [tolerance=±5% resistance=10k package="2010 [SMD]"]
  12V = Power plug
  Relé1 = KY-019 5V Relay Module [package="Breakout board"]
  Relé2 = KY-019 5V Relay Module [package="Breakout board"]
  12V_to_10V = LM2596 step down module

nets:
  N1: Componente1.A3, Componente2.S
  N2: Componente1.A4/SDA, ZS-042_RTC1.SDA, OLED_I2C1.SDA
  N3: Componente1.A5/SCL, ZS-042_RTC1.SCL, OLED_I2C1.SCK
  N4: Componente1.D8, S3.1, R3.Pin_1
  N5: Componente1.D9_PWM, S2.1, R2.Pin_1
  N6: Componente1.D10_PWM/SS, S1.1, R1.Pin_1
  N7: Componente1.D12/MISO, Relé1.S
  N8: Componente1.D13/SCK, Relé2.S
  GND: Componente1.GND, Componente2.GND, Componente2.-, ZS-042_RTC1.GND, OLED_I2C1.GND, R1.Pin_0, R2.Pin_0, R3.Pin_0, 12V.GND, Relé1.-, Relé2.-, 12V_to_10V.IN-, 12V_to_10V.OUT-
  VCC: Componente1.5V, Componente2.VCC, Componente2.+, OLED_I2C1.VDD, S1.3, 12V.VCC, 12V_to_10V.IN+
  N9: Componente1.VIN, 12V_to_10V.OUT+
  N10: ZS-042_RTC1.VCC, S3.3, Relé1.+, Relé2.+
  N11: S1.2, C1.1
  N12: S1.4, C1.2, S2.4, S3.4, C2.2, C3.2
  N13: S2.2, C2.1
  N14: S3.2, C3.1

custom parts:
  KY-019 5V Relay Module: KY-019 5V Relay module, used to control AC circuits.
  LM2596 step down module: LM2596 DC-DC step down power supply module 3 A.
